# Fritzing sketch schematics (saved by Fritzing 0.9.3b)
perfboards: 7
stripboards: 1

parts:
  Q3 = NPN-Transistor [package="TO92 [THT]"]
  Q2 = NPN-Transistor [package="TO92 [THT]"]
  Q1 = NPN-Transistor [package="TO92 [THT]"]
  R3 = Resistor [tolerance=±5% resistance=10k package=THT]
  R2 = Resistor [tolerance=±5% resistance=10k package=THT]
  R1 = Resistor [tolerance=±5% resistance=10k package=THT]
  R6 = Resistor [tolerance=±5% resistance=56 package=THT]
  R5 = Resistor [tolerance=±5% resistance=39 package=THT]
  R4 = Resistor [tolerance=±5% resistance=56 package=THT]
  LED3 = LED - 5mm [color="Red (633nm)" package="5 mm [THT]"]
  LED2 = LED - 5mm [color="Green (565nm)" package="5 mm [THT]"]
  LED1 = LED - 5mm [color="Red (633nm)" package="5 mm [THT]"]
  IC1 = IC, DIP package, 28 pins [chip_label=MCP23017]
  R7 = Resistor [tolerance=±5% resistance=10k package=THT]
  R8 = Resistor [tolerance=±5% resistance=10k package=THT]
  R9 = Resistor [tolerance=±5% resistance=10k package=THT]
  R10 = Resistor [tolerance=±5% resistance=10k package=THT]
  R11 = Resistor [tolerance=±5% resistance=10k package=THT]
  R12 = Resistor [tolerance=±5% resistance=10k package=THT]
  R13 = Resistor [tolerance=±5% resistance=10k package=THT]
  R14 = Resistor [tolerance=±5% resistance=10k package=THT]
  R15 = Resistor [tolerance=±5% resistance=10k package=THT]
  R16 = Resistor [tolerance=±5% resistance=10k package=THT]
  R17 = Resistor [tolerance=±5% resistance=10k package=THT]
  R18 = Resistor [tolerance=±5% resistance=10k package=THT]
  R20 = Resistor [tolerance=±5% resistance=10k package=THT]
  R21 = Resistor [tolerance=±5% resistance=10k package=THT]
  R22 = Resistor [tolerance=±5% resistance=10k package=THT]
  R23 = Resistor [tolerance=±5% resistance=10k package=THT]
  R24 = Resistor [tolerance=±5% resistance=10k package=THT]
  R25 = Resistor [tolerance=±5% resistance=10k package=THT]
  R26 = Resistor [tolerance=±5% resistance=10k package=THT]
  R27 = Resistor [tolerance=±5% resistance=10k package=THT]
  R28 = Resistor [tolerance=±5% resistance=10k package=THT]
  R29 = Resistor [tolerance=±5% resistance=10k package=THT]
  R30 = Resistor [tolerance=±5% resistance=10k package=THT]
  R31 = Resistor [tolerance=±5% resistance=10k package=THT]
  R32 = Resistor [tolerance=±5% resistance=10k package=THT]
  R33 = Resistor [tolerance=±5% resistance=10k package=THT]
  R34 = Resistor [tolerance=±5% resistance=10k package=THT]
  R35 = Resistor [tolerance=±5% resistance=10k package=THT]
  R36 = Resistor [tolerance=±5% resistance=10k package=THT]
  R37 = Resistor [tolerance=±5% resistance=10k package=THT]
  R38 = Resistor [tolerance=±5% resistance=10k package=THT]
  C1 = Ceramic Capacitor [capacitance=100nF package="100 mil [THT, multilayer]"]
  C2 = Ceramic Capacitor [capacitance=100nF package="100 mil [THT, multilayer]"]
  C3 = Ceramic Capacitor [capacitance=100nF package="100 mil [THT, multilayer]"]
  C4 = Ceramic Capacitor [capacitance=100nF package="100 mil [THT, multilayer]"]
  C5 = Ceramic Capacitor [capacitance=100nF package="100 mil [THT, multilayer]"]
  C6 = Ceramic Capacitor [capacitance=100nF package="100 mil [THT, multilayer]"]
  C7 = Ceramic Capacitor [capacitance=100nF package="100 mil [THT, multilayer]"]
  C8 = Ceramic Capacitor [capacitance=100nF package="100 mil [THT, multilayer]"]
  C9 = Ceramic Capacitor [capacitance=100nF package="100 mil [THT, multilayer]"]
  J9 = male pin header, 3 pins [form="♂ (male)"]
  C10 = Ceramic Capacitor [capacitance=100nF package="100 mil [THT, multilayer]"]
  C11 = Ceramic Capacitor [capacitance=100nF package="100 mil [THT, multilayer]"]
  C12 = Ceramic Capacitor [capacitance=100nF package="100 mil [THT, multilayer]"]
  C13 = Ceramic Capacitor [capacitance=100nF package="100 mil [THT, multilayer]"]
  C14 = Ceramic Capacitor [capacitance=100nF package="100 mil [THT, multilayer]"]
  C15 = Ceramic Capacitor [capacitance=100nF package="100 mil [THT, multilayer]"]
  C16 = Ceramic Capacitor [capacitance=100nF package="100 mil [THT, multilayer]"]
  C17 = Ceramic Capacitor [capacitance=100nF package="100 mil [THT, multilayer]"]
  R19 = Resistor [tolerance=±5% resistance=10k package=THT]
  J10 = male pin header, 3 pins [form="♂ (male)"]
  J11 = male pin header, 3 pins [form="♂ (male)"]
  J12 = male pin header, 3 pins [form="♂ (male)"]
  J13 = male pin header, 3 pins [form="♂ (male)"]
  R39 = Resistor [tolerance=±5% resistance=10k package=THT]
  J14 = shrouded pin header, 8 pins [form="♂ (shrouded male)"]
  J15 = shrouded pin header, 8 pins [form="♂ (shrouded male)"]
  R40 = Resistor [tolerance=±5% resistance=10k package=THT]
  R41 = Resistor [tolerance=±5% resistance=10k package=THT]
  R42 = Resistor [tolerance=±5% resistance=10k package=THT]
  R43 = Resistor [tolerance=±5% resistance=10k package=THT]
  R44 = Resistor [tolerance=±5% resistance=10k package=THT]
  R45 = Resistor [tolerance=±5% resistance=10k package=THT]
  R46 = Resistor [tolerance=±5% resistance=10k package=THT]
  R47 = Resistor [tolerance=±5% resistance=10k package=THT]
  R48 = Resistor [tolerance=±5% resistance=10k package=THT]
  R49 = Resistor [tolerance=±5% resistance=10k package=THT]
  R50 = Resistor [tolerance=±5% resistance=10k package=THT]
  R51 = Resistor [tolerance=±5% resistance=10k package=THT]
  R52 = Resistor [tolerance=±5% resistance=10k package=THT]
  R53 = Resistor [tolerance=±5% resistance=10k package=THT]
  R54 = Resistor [tolerance=±5% resistance=10k package=THT]
  R55 = Resistor [tolerance=±5% resistance=10k package=THT]
  R56 = Resistor [tolerance=±5% resistance=10k package=THT]
  R57 = Resistor [tolerance=±5% resistance=10k package=THT]
  R58 = Resistor [tolerance=±5% resistance=10k package=THT]
  R59 = Resistor [tolerance=±5% resistance=10k package=THT]
  R60 = Resistor [tolerance=±5% resistance=10k package=THT]
  R61 = Resistor [tolerance=±5% resistance=10k package=THT]
  R62 = Resistor [tolerance=±5% resistance=10k package=THT]
  R63 = Resistor [tolerance=±5% resistance=10k package=THT]
  R65 = Resistor [tolerance=±5% resistance=10k package=THT]
  R66 = Resistor [tolerance=±5% resistance=10k package=THT]
  R67 = Resistor [tolerance=±5% resistance=10k package=THT]
  R68 = Resistor [tolerance=±5% resistance=10k package=THT]
  R69 = Resistor [tolerance=±5% resistance=10k package=THT]
  R70 = Resistor [tolerance=±5% resistance=10k package=THT]
  R71 = Resistor [tolerance=±5% resistance=10k package=THT]
  R72 = Resistor [tolerance=±5% resistance=10k package=THT]
  IC2 = IC, DIP package, 28 pins [chip_label=MCP23017]
  C18 = Ceramic Capacitor [capacitance=100nF package="100 mil [THT, multilayer]"]
  C19 = Ceramic Capacitor [capacitance=100nF package="100 mil [THT, multilayer]"]
  C20 = Ceramic Capacitor [capacitance=100nF package="100 mil [THT, multilayer]"]
  C21 = Ceramic Capacitor [capacitance=100nF package="100 mil [THT, multilayer]"]
  C22 = Ceramic Capacitor [capacitance=100nF package="100 mil [THT, multilayer]"]
  C23 = Ceramic Capacitor [capacitance=100nF package="100 mil [THT, multilayer]"]
  C24 = Ceramic Capacitor [capacitance=100nF package="100 mil [THT, multilayer]"]
  C25 = Ceramic Capacitor [capacitance=100nF package="100 mil [THT, multilayer]"]
  C26 = Ceramic Capacitor [capacitance=100nF package="100 mil [THT, multilayer]"]
  C27 = Ceramic Capacitor [capacitance=100nF package="100 mil [THT, multilayer]"]
  C28 = Ceramic Capacitor [capacitance=100nF package="100 mil [THT, multilayer]"]
  C29 = Ceramic Capacitor [capacitance=100nF package="100 mil [THT, multilayer]"]
  C30 = Ceramic Capacitor [capacitance=100nF package="100 mil [THT, multilayer]"]
  C31 = Ceramic Capacitor [capacitance=100nF package="100 mil [THT, multilayer]"]
  C32 = Ceramic Capacitor [capacitance=100nF package="100 mil [THT, multilayer]"]
  C33 = Ceramic Capacitor [capacitance=100nF package="100 mil [THT, multilayer]"]
  C34 = Ceramic Capacitor [capacitance=100nF package="100 mil [THT, multilayer]"]
  J16 = shrouded pin header, 16 pins [form="♂ (shrouded male)"]
  J17 = shrouded pin header, 8 pins [form="♂ (shrouded male)"]
  R73 = Resistor [tolerance=±5% resistance=10k package=THT]
  R74 = Resistor [tolerance=±5% resistance=10k package=THT]
  R75 = Resistor [tolerance=±5% resistance=10k package=THT]
  R76 = Resistor [tolerance=±5% resistance=10k package=THT]
  C36 = Ceramic Capacitor [capacitance=100nF package="100 mil [THT, multilayer]"]
  C37 = Ceramic Capacitor [capacitance=100nF package="100 mil [THT, multilayer]"]
  J18 = Raspberry Pi 3 connector - 40 pins [form="♂ (shrouded male)" package=THT]
  J20 = shrouded pin header, 8 pins [form="♂ (shrouded male)"]
  J21 = shrouded pin header, 8 pins [form="♂ (shrouded male)"]
  J22 = shrouded pin header, 8 pins [form="♂ (shrouded male)"]
  IC3 = IC, DIP package, 16 pins [chip_label=MCP3008]
  R77 = Resistor [tolerance=±5% resistance=1.5k package=THT]
  C38 = Ceramic Capacitor [capacitance=1µF package="100 mil [THT, multilayer]"]
  C39 = Ceramic Capacitor [capacitance=1µF package="100 mil [THT, multilayer]"]
  C40 = Ceramic Capacitor [capacitance=100nF package="100 mil [THT, multilayer]"]
  C41 = Ceramic Capacitor [capacitance=100nF package="100 mil [THT, multilayer]"]
  C42 = Ceramic Capacitor [capacitance=100nF package="100 mil [THT, multilayer]"]
  J23 = male pin header, 3 pins [form="♂ (male)"]
  J24 = male pin header, 3 pins [form="♂ (male)"]
  J25 = male pin header, 3 pins [form="♂ (male)"]
  J6 = male pin header, 4 pins [form="♂ (male)"]
  J7 = male pin header, 4 pins [form="♂ (male)"]
  R79 = Resistor [tolerance=±5% resistance=1M package=THT]
  R81 = Resistor [tolerance=±5% resistance=1M package=THT]
  R82 = Resistor [tolerance=±5% resistance=1M package=THT]
  J3 = male pin header, 5 pins [form="♂ (male)"]
  J26 = male pin header, 5 pins [form="♂ (male)"]
  J27 = male pin header, 3 pins [form="♂ (male)"]
  J28 = male pin header, 4 pins [form="♂ (male)"]
  J29 = male pin header, 4 pins [form="♂ (male)"]
  R83 = Rotary Potentiometer (Small) [maximum_resistance=100kΩ package=THT]
  J32 = male pin header, 1 pin [form="♂ (male)"]
  J33 = male pin header, 1 pin [form="♂ (male)"]
  J34 = male pin header, 1 pin [form="♂ (male)"]
  J35 = male pin header, 1 pin [form="♂ (male)"]
  R84 = Rotary Potentiometer (Small) [maximum_resistance=100kΩ package=THT]
  IC4 = IC, DIP package, 14 pins [chip_label=74HC08]
  J36 = male pin header, 8 pins [form="♂ (male)"]
  C43 = Ceramic Capacitor [capacitance=100nF package="100 mil [THT, multilayer]"]
  J37 = male pin header, 2 pins [form="♂ (male)"]
  J38 = male pin header, 3 pins [form="♂ (male)"]
  R85 = Rotary Potentiometer (Small) [maximum_resistance=100kΩ package=THT]
  R86 = Rotary Potentiometer (Small) [maximum_resistance=100kΩ package=THT]
  J39 = male pin header, 3 pins [form="♂ (male)"]
  R87 = Rotary Potentiometer (Small) [maximum_resistance=100kΩ package=THT]
  J40 = male pin header, 3 pins [form="♂ (male)"]
  R89 = Rotary Potentiometer (Small) [maximum_resistance=100kΩ package=THT]
  R88 = Rotary Potentiometer (Small) [maximum_resistance=100kΩ package=THT]
  J41 = male pin header, 3 pins [form="♂ (male)"]
  J42 = male pin header, 3 pins [form="♂ (male)"]
  J44 = male pin header, 3 pins [form="♂ (male)"]
  R90 = Resistor [tolerance=±5% resistance=2.2 package=THT]
  C44 = Electrolytic Capacitor [capacitance=4.7mF package="300 mil [THT, electrolytic]"]
  C45 = Ceramic Capacitor [capacitance="100 nF" package="200 mil [THT, multilayer]"]

nets:
  N1: Q3.E, Q2.E, Q1.E, J3.pin1
  N2: Q3.B, R3.Pin_1
  N3: Q3.C, R6.Pin_1
  N4: Q2.B, R2.Pin_1
  N5: Q2.C, R5.Pin_1
  N6: Q1.B, R1.Pin_1
  N7: Q1.C, R4.Pin_1
  N8: R3.Pin_0, J3.pin2
  N9: R2.Pin_0, J3.pin3
  N10: R1.Pin_0, J3.pin4
  N11: R6.Pin_0, LED3.cathode
  N12: R5.Pin_0, LED2.cathode
  N13: R4.Pin_0, LED1.cathode
  N14: LED3.anode, LED2.anode, LED1.anode, J3.pin5
  N15: IC1.pin1, R23.Pin_1, C1.1
  N16: IC1.pin2, R24.Pin_1, C2.1
  N17: IC1.pin3, R25.Pin_1, C3.1
  N18: IC1.pin4, R26.Pin_1, C4.1
  N19: IC1.pin5, R27.Pin_1, C5.1
  N20: IC1.pin6, R28.Pin_1, C6.1
  N21: IC1.pin7, R29.Pin_1, C7.1
  N22: IC1.pin8, R30.Pin_1, C8.1
  N23: IC1.pin9, R7.Pin_1, R8.Pin_1, R9.Pin_1, R10.Pin_1, R11.Pin_1, R12.Pin_1, R13.Pin_1, R14.Pin_1, R15.Pin_0, R16.Pin_0, R17.Pin_0, R18.Pin_0, R20.Pin_0, R21.Pin_0, R22.Pin_0, C9.1, R19.Pin_0, R39.Pin_1, J14.pin2
  N24: IC1.pin10, IC1.pin16, IC1.pin17, C1.0, C2.0, C3.0, C4.0, C5.0, C6.0, C7.0, C8.0, C9.0, J9.pin1, C10.1, C11.1, C12.1, C13.1, C14.1, C15.1, C16.1, C17.1, J10.pin1, J11.pin1, J12.pin1, J13.pin1, J14.pin1, J6.pin1, J7.pin1
  N25: IC1.pin12, J14.pin5
  N26: IC1.pin13, J14.pin6
  N27: IC1.pin15, R39.Pin_0
  N28: IC1.pin18, J14.pin4
  N29: IC1.pin20, J14.pin3
  N30: IC1.pin21, R38.Pin_0, C17.0
  N31: IC1.pin22, R37.Pin_0, C16.0
  N32: IC1.pin23, R36.Pin_0, C15.0
  N33: IC1.pin24, R35.Pin_0, C14.0
  N34: IC1.pin25, R34.Pin_0, C13.0
  N35: IC1.pin26, R33.Pin_0, C12.0
  N36: IC1.pin27, R32.Pin_0, C11.0
  N37: IC1.pin28, R31.Pin_0, C10.0
  N38: R7.Pin_0, R23.Pin_0, J9.pin2
  N39: R8.Pin_0, R24.Pin_0, J9.pin3
  N40: R9.Pin_0, R25.Pin_0, J7.pin2
  N41: R10.Pin_0, R26.Pin_0, J7.pin3
  N42: R11.Pin_0, R27.Pin_0, J7.pin4
  N43: R12.Pin_0, R28.Pin_0, J6.pin2
  N44: R13.Pin_0, R29.Pin_0, J6.pin3
  N45: R14.Pin_0, R30.Pin_0, J6.pin4
  N46: R15.Pin_1, R31.Pin_1, J13.pin3
  N47: R16.Pin_1, R32.Pin_1, J13.pin2
  N48: R17.Pin_1, R33.Pin_1, J12.pin3
  N49: R18.Pin_1, R34.Pin_1, J12.pin2
  N50: R20.Pin_1, R36.Pin_1, J11.pin2
  N51: R21.Pin_1, R37.Pin_1, J10.pin3
  N52: R22.Pin_1, R38.Pin_1, J10.pin2
  N53: R35.Pin_1, R19.Pin_1, J11.pin3
  N54: J15.pin1, IC2.pin10, IC2.pin15, IC2.pin16, IC2.pin17, C18.0, C19.1, C20.1, C21.1, C22.1, C23.1, C24.1, C25.1, C26.1, C27.0, C28.0, C29.0, C30.0, C31.0, C32.0, C33.0, C34.0, J16.pin1, J16.pin2, J16.pin3, J16.pin16, J17.pin4, J17.pin5, C36.0, C37.0
  N55: J15.pin2, R56.Pin_0, R57.Pin_0, R58.Pin_0, R59.Pin_0, R60.Pin_0, R61.Pin_0, R62.Pin_0, R63.Pin_0, R65.Pin_1, R66.Pin_1, R67.Pin_1, R68.Pin_1, R69.Pin_1, R70.Pin_1, R71.Pin_1, R72.Pin_1, IC2.pin9, C34.1, R75.Pin_1, R76.Pin_1
  N56: J15.pin3, IC2.pin20
  N57: J15.pin4, IC2.pin18
  N58: J15.pin5, IC2.pin12
  N59: J15.pin6, IC2.pin13
  N60: J15.pin7, R73.Pin_1, C36.1
  N61: J15.pin8, R74.Pin_1, C37.1
  N62: R40.Pin_0, IC2.pin21, C19.0
  N63: R40.Pin_1, R56.Pin_1, J16.pin15
  N64: R41.Pin_0, IC2.pin22, C20.0
  N65: R41.Pin_1, R57.Pin_1, J16.pin14
  N66: R42.Pin_0, IC2.pin23, C21.0
  N67: R42.Pin_1, R58.Pin_1, J16.pin13
  N68: R43.Pin_0, IC2.pin24, C22.0
  N69: R43.Pin_1, R59.Pin_1, J16.pin12
  N70: R44.Pin_0, IC2.pin25, C23.0
  N71: R44.Pin_1, R60.Pin_1, J16.pin11
  N72: R45.Pin_0, IC2.pin26, C24.0
  N73: R45.Pin_1, R61.Pin_1, J16.pin10
  N74: R46.Pin_0, IC2.pin27, C25.0
  N75: R46.Pin_1, R62.Pin_1, J16.pin9
  N76: R47.Pin_0, IC2.pin28, C26.0
  N77: R47.Pin_1, R63.Pin_1, J16.pin8
  N78: R48.Pin_0, R65.Pin_0, J16.pin4
  N79: R48.Pin_1, IC2.pin8, C18.1
  N80: R49.Pin_0, R66.Pin_0, J16.pin5
  N81: R49.Pin_1, IC2.pin7, C27.1
  N82: R50.Pin_0, R67.Pin_0, J16.pin6
  N83: R50.Pin_1, IC2.pin6, C28.1
  N84: R51.Pin_0, R68.Pin_0, J16.pin7
  N85: R51.Pin_1, IC2.pin5, C29.1
  N86: R52.Pin_0, R69.Pin_0, J17.pin8
  N87: R52.Pin_1, IC2.pin4, C30.1
  N88: R53.Pin_0, R70.Pin_0, J17.pin1
  N89: R53.Pin_1, IC2.pin3, C31.1
  N90: R54.Pin_0, R71.Pin_0, J17.pin2
  N91: R54.Pin_1, IC2.pin2, C32.1
  N92: R55.Pin_0, R72.Pin_0, J17.pin3
  N93: R55.Pin_1, IC2.pin1, C33.1
  N94: J17.pin6, R73.Pin_0, R75.Pin_0
  N95: J17.pin7, R74.Pin_0, R76.Pin_0
  N96: J18.01, J20.pin2, J21.pin7, J27.pin1
  N97: J18.03, J20.pin6, J21.pin3
  N98: J18.05, J20.pin5, J21.pin4
  N99: J18.07, J20.pin7
  N100: J18.09, J20.pin1, J21.pin8, J26.pin1
  N101: J18.11, J26.pin2
  N102: J18.13, J26.pin3
  N103: J18.15, J26.pin4
  N104: J18.17, IC3.pin16, R77.Pin_0, C38.0, J26.pin5
  N105: J18.19, J22.pin4, IC3.pin11
  N106: J18.21, IC3.pin12
  N107: J18.23, J22.pin3, IC3.pin13
  N108: J18.29, J21.pin6
  N109: J18.39, J22.pin8, IC3.pin1, IC3.pin2, IC3.pin6, IC3.pin7, IC3.pin8, IC3.pin9, IC3.pin14, C38.1, C39.1, C40.1, C41.1, C42.1, J23.pin1, J24.pin1, J25.pin1, R79.Pin_1, R81.Pin_1, R82.Pin_0
  N110: J18.24, IC3.pin10
  N111: J18.22, J20.pin8
  N112: J18.18, J20.pin4, J21.pin5, J22.pin7
  N113: J18.16, J22.pin6
  N114: J18.12, J22.pin5
  N115: J18.08, J20.pin3
  N116: J18.06, J37.pin1, J37.pin2
  N117: J18.02, J27.pin3
  N118: J22.pin1, J22.pin2, J27.pin2
  N119: IC3.pin3, C40.0, J23.pin3, R82.Pin_1
  N120: IC3.pin4, C41.0, J24.pin3, R81.Pin_0
  N121: IC3.pin5, C42.0, J25.pin3, R79.Pin_0
  N122: IC3.pin15, R77.Pin_1, C39.0, J23.pin2, J24.pin2, J25.pin2
  N123: J28.pin1, R84.leg1
  N124: J28.pin2, J33.pin1, R84.wiper
  N125: J28.pin3, R84.leg2
  N126: J28.pin4, J32.pin1
  N127: J29.pin1, R83.leg1
  N128: J29.pin2, R83.wiper, J35.pin1
  N129: J29.pin3, R83.leg2
  N130: J29.pin4, J34.pin1
  N131: IC4.pin1, IC4.pin4, IC4.pin9, IC4.pin10, J36.pin2
  N132: IC4.pin2, J36.pin3
  N133: IC4.pin3, J36.pin4
  N134: IC4.pin5, J36.pin6
  N135: IC4.pin6, J36.pin7
  N136: IC4.pin7, IC4.pin12, IC4.pin13, J36.pin8, C43.1, J44.pin1
  N137: IC4.pin8, J44.pin3
  N138: IC4.pin14, J36.pin1, C43.0, J44.pin2
  N139: J38.pin1, R85.leg1
  N140: J38.pin2, R85.wiper
  N141: J38.pin3, R85.leg2
  N142: R86.leg1, J39.pin1
  N143: R86.wiper, J39.pin2
  N144: R86.leg2, J39.pin3
  N145: R87.leg1, J40.pin1
  N146: R87.wiper, J40.pin2
  N147: R87.leg2, J40.pin3
  N148: R89.leg1, J42.pin1
  N149: R89.wiper, J42.pin2
  N150: R89.leg2, J42.pin3
  N151: R88.leg1, J41.pin1
  N152: R88.wiper, J41.pin2
  N153: R88.leg2, J41.pin3
  +5V Tranfo: R90.Pin_0
  +5V USB: R90.Pin_1, C44.+, C45.0
  GND: C44.-, C45.1

notes:
  Hole
  Main board
  This connector ↑ is mirrored
  LEDs are mounted on the copper side
  LED board
  Incremental encoder board
  Switch board
  Incremental encoders are mounted on the copper side
  Incremental encoders with push buttons
  Incremental encoders
  Display fix board
  Switch board →
  Rot. enc. board
  LED board →
  Display boards →
  ↑ Expression 1 2 3
  ↓ Footswitches
  ↑ UI switches
  ← RPi3
  ← Rot. enc. A4
  ← Rot. enc. A1
  ← Rot. enc. A5
  ← Rot. enc. B1
  ← Rot. enc. B2
  Transfo
  USB
  Power supply filter

custom parts:
  Raspberry Pi 3 connector - 40 pins: Raspberry Pi 3 connector
